# Fritzing sketch PPBalance - Manual Control (saved by Fritzing 0.9.4)
breadboards: 1

parts:
  Part1 = Arduino Uno (Rev3)
  J1 = Basic Servo
  S1 = Square Pushbutton
  S2 = Square Pushbutton
  S3 = Square Pushbutton
  S4 = Square Pushbutton
  J2 = Infrared Proximity Sensor
  U1 = POT [package=pot_mammoth]
  U2 = POT [package=pot_mammoth]
  U3 = POT [package=pot_mammoth]
  U4 = POT [package=pot_mammoth]
  C1 = Capacitor [package=cap-pth-small2]
  C2 = Capacitor Polarized [package=panasonic_d]

nets:
  N1: Part1.A0, J2.Vout
  N2: Part1.A1, U1.A
  N3: Part1.A2, U2.A
  N4: Part1.A3, U3.A
  N5: Part1.A4/SDA, U4.A
  N6: Part1.D9_PWM, J1.pulse
  N7: Part1.D10_PWM/SS, S1.leg0
  N8: Part1.D11_PWM/MOSI, S2.leg0
  N9: Part1.D12/MISO, S3.leg0
  N10: Part1.D13/SCK, S4.leg0
  GND: Part1.GND, J1.gnd, J2.GND, U1.S, U2.S, U3.S, U4.S, C1.1, C2.-
  VCC: Part1.5V, J1.vcc, S1.leg1, S2.leg1, S3.leg1, S4.leg1, J2.Vcc, U1.E, U2.E, U3.E, U4.E, C1.2, C2.+
